# Fritzing sketch 3ZoneTermostat_v0.4.0 (saved by Fritzing 0.9.3b)
breadboards: 1

parts:
  Součástka1 = Arduino Uno (Rev3)
  U1 = RF-LINK_RX [package=rf-link_rx]
  ANT1 = Antenna
  IC1 = DS3231MZ Real Time Clock
  Součástka2 = DeuLigne 1.1 - The Snootlab's LCD shield for Arduino
  U2 = mystery part, 6 pins [chip_label="relay HL-51"]

nets:
  N1: Součástka1.A0, Součástka2.A0
  N2: Součástka1.A4/SDA, IC1.Pin_7, Součástka2.A4(SDA)
  N3: Součástka1.A5/SCL, IC1.Pin_8, Součástka2.A5(CLK)
  N4: Součástka1.D8, Součástka2.D8
  N5: Součástka1.D9_PWM, Součástka2.D9
  N6: Součástka1.D10_PWM/SS, Součástka2.D10_SS
  N7: Součástka1.D11_PWM/MOSI, Součástka2.D11_MOSI, U2.pin2
  GND: Součástka1.GND, U1.GND, IC1.Pin_5, Součástka2.GND, U2.pin3
  N8: Součástka1.D2, U1.DATA, Součástka2.D2
  N9: Součástka1.D4, Součástka2.D4
  N10: Součástka1.D5_PWM, Součástka2.D5
  N11: Součástka1.D6_PWM, Součástka2.D6
  N12: Součástka1.D7, Součástka2.D7
  N13: Součástka1.RESET, Součástka2.RESET
  +5V: Součástka1.5V, U1.+5V, IC1.Pin_2, Součástka2.+5V, U2.pin1
  N14: U1.ANT, ANT1.antenna_lead

custom parts:
  DS3231MZ Real Time Clock: DS3231MZ Real Time Clock. SO-8 surface mount version.
